# Fritzing sketch IWT-SketchReedSwitch (saved by Fritzing 0.9.3b)
circuit board: 8.46667cm x 5.64444cm

parts:
  J2 = female pin header, 8 pins [form="♀ (female)"]
  Componente1 = Adafruit 1.54" Tri-Color eInk / ePaper Display with SRAM [part_number=3625]
  Mod1 = azure-sphere_1
  Reed_Switch = SWITCH-MOMENTARY-2 [package=reed_switch_plastic]  # not connected
  R1 = Resistor [tolerance=±5% resistance=4.7k package=THT]  # not connected

nets (from the schematic view):
  N1: J2.pin1, Mod1.connector8
  N2: J2.pin2, Mod1.connector9
  N3: J2.pin3, Mod1.connector10
  N4: J2.pin4, Mod1.connector11
  N5: J2.pin5, Mod1.connector12
  N6: J2.pin6, Mod1.connector13
  N7: J2.pin7, Mod1.connector14
  N8: J2.pin8, Mod1.connector15
  N9: Componente1.3.3V, Mod1.connector50
  N10: Componente1.GND, Mod1.connector55
  N11: Componente1.SCLK, Mod1.connector3
  N12: Componente1.MOSI, Mod1.connector5
  N13: Componente1.SDCS, Mod1.connector2
  N14: Componente1.RESET, Mod1.connector1
  N15: Componente1.BUSY, Mod1.connector24

notes:
  DISPLAY ---> CLICK
  ------------------------------
  RST | 2 | RST
  CS | 3 | CS
  SCK | 4 | SCK
  SDI | 6 | MOSI
  +3.3V | 7 | 3.3V
  GND | 8 | GND
  ------------------------------
  D / C | 16 | PWM
  BSY | 15 | INT
  ------------------------------

custom parts:
  Adafruit 1.54" Tri-Color eInk / ePaper Display with SRAM: This small 1.54" tri-color display has 152x152 black and red ink pixels and a white-ish background. Using our Arduino library, you can create a 'frame buffer' with what pixels you want to have activated and then write that out to the display. We tossed a small SRAM chip on the back. This chip shares the SPI port the eInk display uses, so you only need one extra pin. And, no more frame-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
